# Fritzing sketch smokedetection (saved by Fritzing 0.9.3b)
breadboards: 1

parts:
  Part1 = Arduino Nano (Rev3.0)
  MQ-2_Gas_Sensor = GAS_SENSOR [package=mq-3]

nets:
  N1: Part1.VIN, MQ-2_Gas_Sensor.A1
  N2: Part1.5V, MQ-2_Gas_Sensor.B1
